// Logisim project Projeto_Chatbot.circ as structural Verilog: 61 circuits, main circuit main
module main (
);

  wire Clock, Falando, Falando_1, Falando_2, Falando_3, Falando_4, Falando_5, Falando_6, Falando_7,
       Falando_8, Falando_9, Falando_10, Falando_11, Falando_12, Falando_13, Falando_14, Falando_15,
       Falando_16, Falando_17, Falando_18, Falando_19, Falando_20, Falando_21, Falando_22, Falando_23,
       Falando_24, Falando_25, Falando_26, Falando_27, Falando_28, Falando_29, Falando_30, Iniciar,
       Iniciar_2, Iniciar_3, Iniciar_4, Iniciar_5, Iniciar_6, Iniciar_7, Iniciar_8, Iniciar_9, Iniciar_10,
       Iniciar_11, Iniciar_12, Iniciar_13, Iniciar_14, Iniciar_15, Iniciar_16, Iniciar_17, Iniciar_18,
       Iniciar_19, Iniciar_20, Iniciar_21, Iniciar_22, Iniciar_23, Iniciar_24, Iniciar_25, Iniciar_26,
       Iniciar_27, Iniciar_28, Iniciar_29, Iniciar_30, keyboard_1_avail, or_3_out, Reset, Reset_2_out,
       Reset_out;
  wire [6:0] Barramento, Char;

  Clock clock_1 (.out(Clock));
  Keyboard keyboard_1 (.clk(Clock), .re(1'b1), .avail(keyboard_1_avail), .data(Char));  // open: clr
  Button u_Reset (.out(Reset_out));
  assign Barramento = keyboard_1_avail ? Char : 7'bz;  // Controlled_Buffer controlled_buffer_1
  or or_1 (Reset, Reset_out, Falando);
  or or_2 (Falando, Falando_1, Falando_2, Falando_3, Falando_4, Falando_5, Falando_6, Falando_7, Falando_8, Falando_9, Falando_10, Falando_11, Falando_12, Falando_13, Falando_14, Falando_15, Falando_16, Falando_17, Falando_18, Falando_19, Falando_20, Falando_21, Falando_22, Falando_23, Falando_24, Falando_25, Falando_26, Falando_27, Falando_28, Falando_29, Falando_30);
  TTY #(.rows(10), .cols(120)) tty_1 (.data(Barramento), .clk(Clock), .we(or_3_out), .clr(Reset_2_out));
  or or_3 (or_3_out, Falando, keyboard_1_avail);
  Button Reset_2 (.out(Reset_2_out));
  Detector_1 detector_1_1 (.Char_In(Char), .Clock(Clock), .Reset_Externo(Reset), .Frase_Detectada(Iniciar));
  Resposta_1 resposta_1_1 (.Iniciar(Iniciar), .Clock(Clock), .Falando(Falando_1), .Char_Out(Barramento));
  Detector_2 detector_2_1 (.Char_In(Char), .Clock(Clock), .Reset_Externo(Reset), .Frase_Detectada(Iniciar_2));
  Resposta_2 resposta_2_1 (.Iniciar(Iniciar_2), .Clock(Clock), .Falando(Falando_2), .Char_Out(Barramento));
  Detector_3 detector_3_1 (.Char_In(Char), .Clock(Clock), .Reset_Externo(Reset), .Frase_Detectada(Iniciar_3));
  Resposta_3 resposta_3_1 (.Iniciar(Iniciar_3), .Clock(Clock), .Falando(Falando_3), .Char_Out(Barramento));
  Detector_4 detector_4_1 (.Char_In(Char), .Clock(Clock), .Reset_Externo(Reset), .Frase_Detectada(Iniciar_4));
  Resposta_4 resposta_4_1 (.Iniciar(Iniciar_4), .Clock(Clock), .Falando(Falando_4), .Char_Out(Barramento));
  Detector_5 detector_5_1 (.Char_In(Char), .Clock(Clock), .Reset_Externo(Reset), .Frase_Detectada(Iniciar_5));
  Resposta_5 resposta_5_1 (.Iniciar(Iniciar_5), .Clock(Clock), .Falando(Falando_5), .Char_Out(Barramento));
  Detector_6 detector_6_1 (.Char_In(Char), .Clock(Clock), .Reset_Externo(Reset), .Frase_Detectada(Iniciar_6));
  Resposta_6 resposta_6_1 (.Iniciar(Iniciar_6), .Clock(Clock), .Falando(Falando_6), .Char_Out(Barramento));
  Detector_7 detector_7_1 (.Char_In(Char), .Clock(Clock), .Reset_Externo(Reset), .Frase_Detectada(Iniciar_7));
  Resposta_7 resposta_7_1 (.Iniciar(Iniciar_7), .Clock(Clock), .Falando(Falando_7), .Char_Out(Barramento));
  Detector_8 detector_8_1 (.Char_In(Char), .Clock(Clock), .Reset_Externo(Reset), .Frase_Detectada(Iniciar_8));
  Resposta_8 resposta_8_1 (.Iniciar(Iniciar_8), .Clock(Clock), .Falando(Falando_8), .Char_Out(Barramento));
  Detector_9 detector_9_1 (.Char_In(Char), .Clock(Clock), .Reset_Externo(Reset), .Frase_Detectada(Iniciar_9));
  Resposta_9 resposta_9_1 (.Iniciar(Iniciar_9), .Clock(Clock), .Falando(Falando_9), .Char_Out(Barramento));
  Detector_10 detector_10_1 (.Char_In(Char), .Clock(Clock), .Reset_Externo(Reset), .Frase_Detectada(Iniciar_10));
  Resposta_10 resposta_10_1 (.Iniciar(Iniciar_10), .Clock(Clock), .Falando(Falando_10), .Char_Out(Barramento));
  Detector_11 detector_11_1 (.Char_In(Char), .Clock(Clock), .Reset_Externo(Reset), .Frase_Detectada(Iniciar_11));
  Resposta_11 resposta_11_1 (.Iniciar(Iniciar_11), .Clock(Clock), .Falando(Falando_11), .Char_Out(Barramento));
  Detector_12 detector_12_1 (.Char_In(Char), .Clock(Clock), .Reset_Externo(Reset), .Frase_Detectada(Iniciar_12));
  Resposta_12 resposta_12_1 (.Iniciar(Iniciar_12), .Clock(Clock), .Falando(Falando_12), .Char_Out(Barramento));
  Detector_13 detector_13_1 (.Char_In(Char), .Clock(Clock), .Reset_Externo(Reset), .Frase_Detectada(Iniciar_13));
  Resposta_13 resposta_13_1 (.Iniciar(Iniciar_13), .Clock(Clock), .Falando(Falando_13), .Char_Out(Barramento));
  Detector_14 detector_14_1 (.Char_In(Char), .Clock(Clock), .Reset_Externo(Reset), .Frase_Detectada(Iniciar_14));
  Resposta_14 resposta_14_1 (.Iniciar(Iniciar_14), .Clock(Clock), .Falando(Falando_14), .Char_Out(Barramento));
  Detector_15 detector_15_1 (.Char_In(Char), .Clock(Clock), .Reset_Externo(Reset), .Frase_Detectada(Iniciar_15));
  Resposta_15 resposta_15_1 (.Iniciar(Iniciar_15), .Clock(Clock), .Falando(Falando_15), .Char_Out(Barramento));
  Detector_16 detector_16_1 (.Char_In(Char), .Clock(Clock), .Reset_Externo(Reset), .Frase_Detectada(Iniciar_16));
  Resposta_16 resposta_16_1 (.Iniciar(Iniciar_16), .Clock(Clock), .Falando(Falando_16), .Char_Out(Barramento));
  Detector_17 detector_17_1 (.Char_In(Char), .Clock(Clock), .Reset_Externo(Reset), .Frase_Detectada(Iniciar_17));
  Resposta_17 resposta_17_1 (.Iniciar(Iniciar_17), .Clock(Clock), .Falando(Falando_17), .Char_Out(Barramento));
  Detector_18 detector_18_1 (.Char_In(Char), .Clock(Clock), .Reset_Externo(Reset), .Frase_Detectada(Iniciar_18));
  Resposta_18 resposta_18_1 (.Iniciar(Iniciar_18), .Clock(Clock), .Falando(Falando_18), .Char_Out(Barramento));
  Detector_19 detector_19_1 (.Char_In(Char), .Clock(Clock), .Reset_Externo(Reset), .Frase_Detectada(Iniciar_19));
  Resposta_19 resposta_19_1 (.Iniciar(Iniciar_19), .Clock(Clock), .Falando(Falando_19), .Char_Out(Barramento));
  Detector_20 detector_20_1 (.Char_In(Char), .Clock(Clock), .Reset_Externo(Reset), .Frase_Detectada(Iniciar_20));
  Resposta_20 resposta_20_1 (.Iniciar(Iniciar_20), .Clock(Clock), .Falando(Falando_20), .Char_Out(Barramento));
  Detector_27 detector_27_1 (.Char_In(Char), .Clock(Clock), .Reset_Externo(Reset), .Frase_Detectada(Iniciar_27));
  Resposta_27 resposta_27_1 (.Iniciar(Iniciar_27), .Clock(Clock), .Falando(Falando_27), .Char_Out(Barramento));
  Detector_28 detector_28_1 (.Char_In(Char), .Clock(Clock), .Reset_Externo(Reset), .Frase_Detectada(Iniciar_28));
  Resposta_28 resposta_28_1 (.Iniciar(Iniciar_28), .Clock(Clock), .Falando(Falando_28), .Char_Out(Barramento));
  Detector_29 detector_29_1 (.Char_In(Char), .Clock(Clock), .Reset_Externo(Reset), .Frase_Detectada(Iniciar_29));
  Resposta_29 resposta_29_1 (.Iniciar(Iniciar_29), .Clock(Clock), .Falando(Falando_29), .Char_Out(Barramento));
  Detector_30 detector_30_1 (.Char_In(Char), .Clock(Clock), .Reset_Externo(Reset), .Frase_Detectada(Iniciar_30));
  Resposta_30 resposta_30_1 (.Iniciar(Iniciar_30), .Clock(Clock), .Falando(Falando_30), .Char_Out(Barramento));
  Detector_21 detector_21_1 (.Char_In(Char), .Clock(Clock), .Reset_Externo(Reset), .Frase_Detectada(Iniciar_21));
  Resposta_21 resposta_21_1 (.Iniciar(Iniciar_21), .Clock(Clock), .Falando(Falando_21), .Char_Out(Barramento));
  Detector_22 detector_22_1 (.Char_In(Char), .Clock(Clock), .Reset_Externo(Reset), .Frase_Detectada(Iniciar_22));
  Resposta_22 resposta_22_1 (.Iniciar(Iniciar_22), .Clock(Clock), .Falando(Falando_22), .Char_Out(Barramento));
  Detector_23 detector_23_1 (.Char_In(Char), .Clock(Clock), .Reset_Externo(Reset), .Frase_Detectada(Iniciar_23));
  Resposta_23 resposta_23_1 (.Iniciar(Iniciar_23), .Clock(Clock), .Falando(Falando_23), .Char_Out(Barramento));
  Detector_24 detector_24_1 (.Char_In(Char), .Clock(Clock), .Reset_Externo(Reset), .Frase_Detectada(Iniciar_24));
  Resposta_24 resposta_24_1 (.Iniciar(Iniciar_24), .Clock(Clock), .Falando(Falando_24), .Char_Out(Barramento));
  Detector_25 detector_25_1 (.Char_In(Char), .Clock(Clock), .Reset_Externo(Reset), .Frase_Detectada(Iniciar_25));
  Resposta_25 resposta_25_1 (.Iniciar(Iniciar_25), .Clock(Clock), .Falando(Falando_25), .Char_Out(Barramento));
  Detector_26 detector_26_1 (.Char_In(Char), .Clock(Clock), .Reset_Externo(Reset), .Frase_Detectada(Iniciar_26));
  Resposta_26 resposta_26_1 (.Iniciar(Iniciar_26), .Clock(Clock), .Falando(Falando_26), .Char_Out(Barramento));

  // Other names for the same wires on the sheet: Resposta_1[6:0] = Barramento; Resposta_2[6:0] = Barramento;
  //   Resposta_3[6:0] = Barramento; Resposta_4[6:0] = Barramento; Resposta_5[6:0] = Barramento;
  //   Resposta_6[6:0] = Barramento; Resposta_7[6:0] = Barramento; Resposta_8[6:0] = Barramento;
  //   Resposta_9[6:0] = Barramento; Resposta_10[6:0] = Barramento; Resposta_11[6:0] = Barramento;
  //   Resposta_12[6:0] = Barramento; Resposta_13[6:0] = Barramento; Resposta_14[6:0] = Barramento;
  //   Resposta_15[6:0] = Barramento; Resposta_16[6:0] = Barramento; Resposta_17[6:0] = Barramento;
  //   Resposta_18[6:0] = Barramento; Resposta_19[6:0] = Barramento; Resposta_20[6:0] = Barramento;
  //   Resposta_21[6:0] = Barramento; Resposta_22[6:0] = Barramento; Resposta_23[6:0] = Barramento;
  //   Resposta_24[6:0] = Barramento; Resposta_25[6:0] = Barramento; Resposta_26[6:0] = Barramento;
  //   Resposta_27[6:0] = Barramento; Resposta_28[6:0] = Barramento; Resposta_29[6:0] = Barramento;
  //   Resposta_30[6:0] = Barramento; Texto[6:0] = Barramento
endmodule

// R1
module Resposta_1 (
  input  Iniciar,
  input  Clock,
  output Falando,
  output [6:0] Char_Out
);

  wire comparator_1_eq;
  wire [6:0] counter_1_q, rom_1_data;

  D_Flip_Flop d_ff_1 (.clk(Clock), .Q(Falando), .preset(Iniciar), .reset(comparator_1_eq));  // open: D, Qn, en
  Counter #(.width(7), .max('h7f)) counter_1 (
    .count(Falando), .Q(counter_1_q), .clk(Clock), .clr(comparator_1_eq));  // open: load, D, carry
  Comparator #(.width(7)) comparator_1 (.a(counter_1_q), .b(7'b0001111), .eq(comparator_1_eq));  // open: gt, lt
  ROM #(.addrWidth(7), .dataWidth(7)) rom_1 (.addr(counter_1_q), .data(rom_1_data));  // open: sel
  assign Char_Out = Falando ? rom_1_data : 7'bz;  // Controlled_Buffer controlled_buffer_1

  // Notes on the sheet:
  //   contents of rom_1 (hex, n*v repeats v):
  //   4f 6c 61 21 20 54 75 64 6f 20 62 65 6d 3f a
endmodule

// D1
module Detector_1 (
  input  [6:0] Char_In,
  input  Clock,
  input  Reset_Externo,
  output Frase_Detectada
);

  wire and_1_out, comparator_2_eq, comparator_3_eq, not_1_out, not_2_out, or_1_out;
  wire [6:0] counter_1_q, rom_1_data;

  Counter #(.width(7), .max('h7f)) counter_1 (
    .count(not_2_out), .Q(counter_1_q), .clk(Clock), .clr(or_1_out));  // open: load, D, carry
  or or_1 (or_1_out, Reset_Externo, and_1_out, Frase_Detectada);
  and and_1 (and_1_out, not_1_out, not_2_out);
  Comparator #(.width(7)) comparator_1 (.a(counter_1_q), .b(7'b0000011), .eq(Frase_Detectada));  // open: gt, lt
  ROM #(.addrWidth(7), .dataWidth(7)) rom_1 (.addr(counter_1_q), .data(rom_1_data));  // open: sel
  Comparator #(.width(7)) comparator_2 (.a(rom_1_data), .b(Char_In), .eq(comparator_2_eq));  // open: gt, lt
  not not_1 (not_1_out, comparator_2_eq);
  not not_2 (not_2_out, comparator_3_eq);
  Comparator #(.width(7)) comparator_3 (.a(Char_In), .b({7{1'b0}}), .eq(comparator_3_eq));  // open: gt, lt

  // Notes on the sheet:
  //   contents of rom_1 (hex, n*v repeats v):
  //   4f 69 a
endmodule

// R2
module Resposta_2 (
  input  Iniciar,
  input  Clock,
  output Falando,
  output [6:0] Char_Out
);

  wire comparator_1_eq;
  wire [6:0] counter_1_q, rom_1_data;

  D_Flip_Flop d_ff_1 (.clk(Clock), .Q(Falando), .preset(Iniciar), .reset(comparator_1_eq));  // open: D, Qn, en
  Counter #(.width(7), .max('h7f)) counter_1 (
    .count(Falando), .Q(counter_1_q), .clk(Clock), .clr(comparator_1_eq));  // open: load, D, carry
  Comparator #(.width(7)) comparator_1 (.a(counter_1_q), .b(7'b1000100), .eq(comparator_1_eq));  // open: gt, lt
  ROM #(.addrWidth(7), .dataWidth(7)) rom_1 (.addr(counter_1_q), .data(rom_1_data));  // open: sel
  assign Char_Out = Falando ? rom_1_data : 7'bz;  // Controlled_Buffer controlled_buffer_1

  // Notes on the sheet:
  //   contents of rom_1 (hex, n*v repeats v):
  //   53 6f 75 20 6f 20 53 61 6d 61 72 53 63 6f 72 65 2c 20 75 6d 20 43 68 61 74 62 6f 74 20 70 72 6f 67
  //   72 61 6d 61 64 6f 20 61 70 65 6e 61 73 20 63 6f 6d 20 6c 6f 67 69 63 61 20 64 69 67 69 74 61 6c 21 a
endmodule

// D2
module Detector_2 (
  input  [6:0] Char_In,
  input  Clock,
  input  Reset_Externo,
  output Frase_Detectada
);

  wire and_1_out, comparator_2_eq, comparator_3_eq, not_1_out, not_2_out, or_1_out;
  wire [6:0] counter_1_q, rom_1_data;

  Counter #(.width(7), .max('h7f)) counter_1 (
    .count(not_2_out), .Q(counter_1_q), .clk(Clock), .clr(or_1_out));  // open: load, D, carry
  or or_1 (or_1_out, Reset_Externo, and_1_out, Frase_Detectada);
  and and_1 (and_1_out, not_1_out, not_2_out);
  Comparator #(.width(7)) comparator_1 (.a(counter_1_q), .b(7'b0010001), .eq(Frase_Detectada));  // open: gt, lt
  ROM #(.addrWidth(7), .dataWidth(7)) rom_1 (.addr(counter_1_q), .data(rom_1_data));  // open: sel
  Comparator #(.width(7)) comparator_2 (.a(rom_1_data), .b(Char_In), .eq(comparator_2_eq));  // open: gt, lt
  not not_1 (not_1_out, comparator_2_eq);
  Comparator #(.width(7)) comparator_3 (.a(Char_In), .b({7{1'b0}}), .eq(comparator_3_eq));  // open: gt, lt
  not not_2 (not_2_out, comparator_3_eq);

  // Notes on the sheet:
  //   contents of rom_1 (hex, n*v repeats v):
  //   51 75 61 6c 20 6f 20 73 65 75 20 6e 6f 6d 65 3f a
endmodule

// R3
module Resposta_3 (
  input  Iniciar,
  input  Clock,
  output Falando,
  output [6:0] Char_Out
);

  wire comparator_1_eq;
  wire [6:0] counter_1_q, rom_1_data;

  D_Flip_Flop d_ff_1 (.clk(Clock), .Q(Falando), .preset(Iniciar), .reset(comparator_1_eq));  // open: D, Qn, en
  Counter #(.width(7), .max('h7f)) counter_1 (
    .count(Falando), .Q(counter_1_q), .clk(Clock), .clr(comparator_1_eq));  // open: load, D, carry
  Comparator #(.width(7)) comparator_1 (.a(counter_1_q), .b(7'b1011101), .eq(comparator_1_eq));  // open: gt, lt
  ROM #(.addrWidth(7), .dataWidth(7)) rom_1 (.addr(counter_1_q), .data(rom_1_data));  // open: sel
  assign Char_Out = Falando ? rom_1_data : 7'bz;  // Controlled_Buffer controlled_buffer_1

  // Notes on the sheet:
  //   contents of rom_1 (hex, n*v repeats v):
  //   45 73 74 65 20 70 72 6f 6a 65 74 6f 20 66 6f 69 20 66 65 69 74 6f 20 70 61 72 61 20 61 20 6d 61 74
  //   65 72 69 61 20 64 65 20 41 72 71 75 69 74 65 74 75 72 61 20 64 65 20 43 6f 6d 70 75 74 61 64 6f 72
  //   65 73 2c 20 64 6f 20 70 72 6f 66 65 73 73 6f 72 20 56 69 6e 69 63 69 75 73 21 a
endmodule

// D3
module Detector_3 (
  input  [6:0] Char_In,
  input  Clock,
  input  Reset_Externo,
  output Frase_Detectada
);

  wire and_1_out, comparator_2_eq, comparator_3_eq, not_1_out, not_2_out, or_1_out;
  wire [6:0] counter_1_q, rom_1_data;

  Counter #(.width(7), .max('h7f)) counter_1 (
    .count(not_2_out), .Q(counter_1_q), .clk(Clock), .clr(or_1_out));  // open: load, D, carry
  or or_1 (or_1_out, Reset_Externo, and_1_out, Frase_Detectada);
  and and_1 (and_1_out, not_1_out, not_2_out);
  Comparator #(.width(7)) comparator_1 (.a(counter_1_q), .b(7'b0001000), .eq(Frase_Detectada));  // open: gt, lt
  ROM #(.addrWidth(7), .dataWidth(7)) rom_1 (.addr(counter_1_q), .data(rom_1_data));  // open: sel
  not not_1 (not_1_out, comparator_2_eq);
  Comparator #(.width(7)) comparator_2 (.a(rom_1_data), .b(Char_In), .eq(comparator_2_eq));  // open: gt, lt
  Comparator #(.width(7)) comparator_3 (.a(Char_In), .b({7{1'b0}}), .eq(comparator_3_eq));  // open: gt, lt
  not not_2 (not_2_out, comparator_3_eq);

  // Notes on the sheet:
  //   contents of rom_1 (hex, n*v repeats v):
  //   50 72 6f 6a 65 74 6f a
endmodule

// R4
module Resposta_4 (
  input  Iniciar,
  input  Clock,
  output Falando,
  output [6:0] Char_Out
);

  wire comparator_1_eq;
  wire [6:0] counter_1_q, rom_1_data;

  D_Flip_Flop d_ff_1 (.clk(Clock), .Q(Falando), .preset(Iniciar), .reset(comparator_1_eq));  // open: D, Qn, en
  Counter #(.width(7), .max('h7f)) counter_1 (
    .count(Falando), .Q(counter_1_q), .clk(Clock), .clr(comparator_1_eq));  // open: load, D, carry
  Comparator #(.width(7)) comparator_1 (.a(counter_1_q), .b(7'b0011011), .eq(comparator_1_eq));  // open: gt, lt
  ROM #(.addrWidth(7), .dataWidth(7)) rom_1 (.addr(counter_1_q), .data(rom_1_data));  // open: sel
  assign Char_Out = Falando ? rom_1_data : 7'bz;  // Controlled_Buffer controlled_buffer_1

  // Notes on the sheet:
  //   contents of rom_1 (hex, n*v repeats v):
  //   45 75 20 74 6f 72 63 6f 20 70 61 72 61 20 6f 20 50 61 6c 6d 65 69 72 61 73 21 a
endmodule

// D4
module Detector_4 (
  input  [6:0] Char_In,
  input  Clock,
  input  Reset_Externo,
  output Frase_Detectada
);

  wire and_1_out, comparator_2_eq, comparator_3_eq, not_1_out, not_2_out, or_1_out;
  wire [6:0] counter_1_q, rom_1_data;

  Counter #(.width(7), .max('h7f)) counter_1 (
    .count(not_2_out), .Q(counter_1_q), .clk(Clock), .clr(or_1_out));  // open: load, D, carry
  or or_1 (or_1_out, Reset_Externo, and_1_out, Frase_Detectada);
  and and_1 (and_1_out, not_1_out, not_2_out);
  Comparator #(.width(7)) comparator_1 (.a(counter_1_q), .b(7'b0010101), .eq(Frase_Detectada));  // open: gt, lt
  ROM #(.addrWidth(7), .dataWidth(7)) rom_1 (.addr(counter_1_q), .data(rom_1_data));  // open: sel
  not not_1 (not_1_out, comparator_2_eq);
  Comparator #(.width(7)) comparator_2 (.a(rom_1_data), .b(Char_In), .eq(comparator_2_eq));  // open: gt, lt
  not not_2 (not_2_out, comparator_3_eq);
  Comparator #(.width(7)) comparator_3 (.a(Char_In), .b({7{1'b0}}), .eq(comparator_3_eq));  // open: gt, lt

  // Notes on the sheet:
  //   contents of rom_1 (hex, n*v repeats v):
  //   51 75 65 20 74 69 6d 65 20 76 6f 63 65 20 74 6f 72 63 65 3f a
endmodule

// R5
module Resposta_5 (
  input  Iniciar,
  input  Clock,
  output Falando,
  output [6:0] Char_Out
);

  wire comparator_1_eq;
  wire [6:0] counter_1_q, rom_1_data;

  D_Flip_Flop d_ff_1 (.clk(Clock), .Q(Falando), .preset(Iniciar), .reset(comparator_1_eq));  // open: D, Qn, en
  Counter #(.width(7), .max('h7f)) counter_1 (
    .count(Falando), .Q(counter_1_q), .clk(Clock), .clr(comparator_1_eq));  // open: load, D, carry
  Comparator #(.width(7)) comparator_1 (.a(counter_1_q), .b(7'b0000110), .eq(comparator_1_eq));  // open: gt, lt
  ROM #(.addrWidth(7), .dataWidth(7)) rom_1 (.addr(counter_1_q), .data(rom_1_data));  // open: sel
  assign Char_Out = Falando ? rom_1_data : 7'bz;  // Controlled_Buffer controlled_buffer_1

  // Notes on the sheet:
  //   contents of rom_1 (hex, n*v repeats v):
  //   53 45 49 53 21 a
endmodule

// D5
module Detector_5 (
  input  [6:0] Char_In,
  input  Clock,
  input  Reset_Externo,
  output Frase_Detectada
);

  wire and_1_out, comparator_2_eq, comparator_3_eq, not_1_out, not_2_out, or_1_out;
  wire [6:0] counter_1_q, rom_1_data;

  Counter #(.width(7), .max('h7f)) counter_1 (
    .count(not_2_out), .Q(counter_1_q), .clk(Clock), .clr(or_1_out));  // open: load, D, carry
  or or_1 (or_1_out, Reset_Externo, and_1_out, Frase_Detectada);
  and and_1 (and_1_out, not_1_out, not_2_out);
  Comparator #(.width(7)) comparator_1 (.a(counter_1_q), .b(7'b0000111), .eq(Frase_Detectada));  // open: gt, lt
  ROM #(.addrWidth(7), .dataWidth(7)) rom_1 (.addr(counter_1_q), .data(rom_1_data));  // open: sel
  not not_1 (not_1_out, comparator_2_eq);
  Comparator #(.width(7)) comparator_2 (.a(rom_1_data), .b(Char_In), .eq(comparator_2_eq));  // open: gt, lt
  Comparator #(.width(7)) comparator_3 (.a(Char_In), .b({7{1'b0}}), .eq(comparator_3_eq));  // open: gt, lt
  not not_2 (not_2_out, comparator_3_eq);

  // Notes on the sheet:
  //   contents of rom_1 (hex, n*v repeats v):
  //   54 72 75 63 6f 21 a
endmodule

// R6
module Resposta_6 (
  input  Iniciar,
  input  Clock,
  output Falando,
  output [6:0] Char_Out
);

  wire comparator_1_eq;
  wire [6:0] counter_1_q, rom_1_data;

  D_Flip_Flop d_ff_1 (.clk(Clock), .Q(Falando), .preset(Iniciar), .reset(comparator_1_eq));  // open: D, Qn, en
  Counter #(.width(7), .max('h7f)) counter_1 (
    .count(Falando), .Q(counter_1_q), .clk(Clock), .clr(comparator_1_eq));  // open: load, D, carry
  Comparator #(.width(7)) comparator_1 (.a(counter_1_q), .b(7'b0000110), .eq(comparator_1_eq));  // open: gt, lt
  ROM #(.addrWidth(7), .dataWidth(7)) rom_1 (.addr(counter_1_q), .data(rom_1_data));  // open: sel
  assign Char_Out = Falando ? rom_1_data : 7'bz;  // Controlled_Buffer controlled_buffer_1

  // Notes on the sheet:
  //   contents of rom_1 (hex, n*v repeats v):
  //   44 4f 5a 45 21 a
endmodule

// D6
module Detector_6 (
  input  [6:0] Char_In,
  input  Clock,
  input  Reset_Externo,
  output Frase_Detectada
);

  wire and_1_out, comparator_2_eq, comparator_3_eq, not_1_out, not_2_out, or_1_out;
  wire [6:0] counter_1_q, rom_1_data;

  Counter #(.width(7), .max('h7f)) counter_1 (
    .count(not_2_out), .Q(counter_1_q), .clk(Clock), .clr(or_1_out));  // open: load, D, carry
  or or_1 (or_1_out, Reset_Externo, and_1_out, Frase_Detectada);
  and and_1 (and_1_out, not_1_out, not_2_out);
  Comparator #(.width(7)) comparator_1 (.a(counter_1_q), .b(7'b0000110), .eq(Frase_Detectada));  // open: gt, lt
  ROM #(.addrWidth(7), .dataWidth(7)) rom_1 (.addr(counter_1_q), .data(rom_1_data));  // open: sel
  not not_1 (not_1_out, comparator_2_eq);
  Comparator #(.width(7)) comparator_2 (.a(rom_1_data), .b(Char_In), .eq(comparator_2_eq));  // open: gt, lt
  Comparator #(.width(7)) comparator_3 (.a(Char_In), .b({7{1'b0}}), .eq(comparator_3_eq));  // open: gt, lt
  not not_2 (not_2_out, comparator_3_eq);

  // Notes on the sheet:
  //   contents of rom_1 (hex, n*v repeats v):
  //   4e 4f 56 45 21 a
endmodule

// R7
module Resposta_7 (
  input  Iniciar,
  input  Clock,
  output Falando,
  output [6:0] Char_Out
);

  wire comparator_1_eq;
  wire [6:0] counter_1_q, rom_1_data;

  D_Flip_Flop d_ff_1 (.clk(Clock), .Q(Falando), .preset(Iniciar), .reset(comparator_1_eq));  // open: D, Qn, en
  Counter #(.width(7), .max('h7f)) counter_1 (
    .count(Falando), .Q(counter_1_q), .clk(Clock), .clr(comparator_1_eq));  // open: load, D, carry
  Comparator #(.width(7)) comparator_1 (.a(counter_1_q), .b(7'b0100100), .eq(comparator_1_eq));  // open: gt, lt
  ROM #(.addrWidth(7), .dataWidth(7)) rom_1 (.addr(counter_1_q), .data(rom_1_data));  // open: sel
  assign Char_Out = Falando ? rom_1_data : 7'bz;  // Controlled_Buffer controlled_buffer_1

  // Notes on the sheet:
  //   contents of rom_1 (hex, n*v repeats v):
  //   45 73 74 6f 75 20 63 6f 6d 20 63 61 73 61 6c 20 6d 61 69 6f 72 2c 20 76 6f 63 65 20 70 65 72 64 65
  //   75 21 a
endmodule

// D7
module Detector_7 (
  input  [6:0] Char_In,
  input  Clock,
  input  Reset_Externo,
  output Frase_Detectada
);

  wire and_1_out, comparator_2_eq, comparator_3_eq, not_1_out, not_2_out, or_1_out;
  wire [6:0] counter_1_q, rom_1_data;

  Counter #(.width(7), .max('h7f)) counter_1 (
    .count(not_2_out), .Q(counter_1_q), .clk(Clock), .clr(or_1_out));  // open: load, D, carry
  or or_1 (or_1_out, Reset_Externo, and_1_out, Frase_Detectada);
  and and_1 (and_1_out, not_1_out, not_2_out);
  Comparator #(.width(7)) comparator_1 (.a(counter_1_q), .b(7'b0000111), .eq(Frase_Detectada));  // open: gt, lt
  ROM #(.addrWidth(7), .dataWidth(7)) rom_1 (.addr(counter_1_q), .data(rom_1_data));  // open: sel
  not not_1 (not_1_out, comparator_2_eq);
  Comparator #(.width(7)) comparator_2 (.a(rom_1_data), .b(Char_In), .eq(comparator_2_eq));  // open: gt, lt
  not not_2 (not_2_out, comparator_3_eq);
  Comparator #(.width(7)) comparator_3 (.a(Char_In), .b({7{1'b0}}), .eq(comparator_3_eq));  // open: gt, lt

  // Notes on the sheet:
  //   contents of rom_1 (hex, n*v repeats v):
  //   44 65 73 63 65 21 a
endmodule

// R8
module Resposta_8 (
  input  Iniciar,
  input  Clock,
  output Falando,
  output [6:0] Char_Out
);

  wire comparator_1_eq;
  wire [6:0] counter_1_q, rom_1_data;

  D_Flip_Flop d_ff_1 (.clk(Clock), .Q(Falando), .preset(Iniciar), .reset(comparator_1_eq));  // open: D, Qn, en
  Counter #(.width(7), .max('h7f)) counter_1 (
    .count(Falando), .Q(counter_1_q), .clk(Clock), .clr(comparator_1_eq));  // open: load, D, carry
  Comparator #(.width(7)) comparator_1 (.a(counter_1_q), .b(7'b0101100), .eq(comparator_1_eq));  // open: gt, lt
  ROM #(.addrWidth(7), .dataWidth(7)) rom_1 (.addr(counter_1_q), .data(rom_1_data));  // open: sel
  assign Char_Out = Falando ? rom_1_data : 7'bz;  // Controlled_Buffer controlled_buffer_1

  // Notes on the sheet:
  //   contents of rom_1 (hex, n*v repeats v):
  //   4f 20 6d 65 6c 68 6f 72 20 6a 6f 67 61 64 6f 72 20 64 6f 20 6d 75 6e 64 6f 20 65 20 6f 20 4c 69 6f
  //   6e 65 6c 20 4d 65 73 73 69 21 a
endmodule

// D8
module Detector_8 (
  input  [6:0] Char_In,
  input  Clock,
  input  Reset_Externo,
  output Frase_Detectada
);

  wire and_1_out, comparator_2_eq, comparator_3_eq, not_1_out, not_2_out, or_1_out;
  wire [6:0] counter_1_q, rom_1_data;

  Counter #(.width(7), .max('h7f)) counter_1 (
    .count(not_2_out), .Q(counter_1_q), .clk(Clock), .clr(or_1_out));  // open: load, D, carry
  or or_1 (or_1_out, Reset_Externo, and_1_out, Frase_Detectada);
  and and_1 (and_1_out, not_1_out, not_2_out);
  Comparator #(.width(7)) comparator_1 (.a(counter_1_q), .b(7'b0100000), .eq(Frase_Detectada));  // open: gt, lt
  ROM #(.addrWidth(7), .dataWidth(7)) rom_1 (.addr(counter_1_q), .data(rom_1_data));  // open: sel
  Comparator #(.width(7)) comparator_2 (.a(rom_1_data), .b(Char_In), .eq(comparator_2_eq));  // open: gt, lt
  not not_1 (not_1_out, comparator_2_eq);
  not not_2 (not_2_out, comparator_3_eq);
  Comparator #(.width(7)) comparator_3 (.a(Char_In), .b({7{1'b0}}), .eq(comparator_3_eq));  // open: gt, lt

  // Notes on the sheet:
  //   contents of rom_1 (hex, n*v repeats v):
  //   51 75 61 6c 20 6f 20 6d 65 6c 68 6f 72 20 6a 6f 67 61 64 6f 72 20 64 6f 20 6d 75 6e 64 6f 3f a
endmodule

// R9
module Resposta_9 (
  input  Iniciar,
  input  Clock,
  output Falando,
  output [6:0] Char_Out
);

  wire comparator_1_eq;
  wire [6:0] counter_1_q, rom_1_data;

  D_Flip_Flop d_ff_1 (.clk(Clock), .Q(Falando), .preset(Iniciar), .reset(comparator_1_eq));  // open: D, Qn, en
  Counter #(.width(7), .max('h7f)) counter_1 (
    .count(Falando), .Q(counter_1_q), .clk(Clock), .clr(comparator_1_eq));  // open: load, D, carry
  Comparator #(.width(7)) comparator_1 (.a(counter_1_q), .b(7'b0100101), .eq(comparator_1_eq));  // open: gt, lt
  ROM #(.addrWidth(7), .dataWidth(7)) rom_1 (.addr(counter_1_q), .data(rom_1_data));  // open: sel
  assign Char_Out = Falando ? rom_1_data : 7'bz;  // Controlled_Buffer controlled_buffer_1

  // Notes on the sheet:
  //   contents of rom_1 (hex, n*v repeats v):
  //   4d 69 6e 68 61 20 73 65 72 69 65 20 66 61 76 6f 72 69 74 61 20 65 20 42 72 65 61 6b 69 6e 67 20 42
  //   61 64 21 a
endmodule

// D9
module Detector_9 (
  input  [6:0] Char_In,
  input  Clock,
  input  Reset_Externo,
  output Frase_Detectada
);

  wire and_1_out, comparator_2_eq, comparator_3_eq, not_1_out, not_2_out, or_1_out;
  wire [6:0] counter_1_q, rom_1_data;

  Counter #(.width(7), .max('h7f)) counter_1 (
    .count(not_2_out), .Q(counter_1_q), .clk(Clock), .clr(or_1_out));  // open: load, D, carry
  or or_1 (or_1_out, Reset_Externo, and_1_out, Frase_Detectada);
  and and_1 (and_1_out, not_1_out, not_2_out);
  Comparator #(.width(7)) comparator_1 (.a(counter_1_q), .b(7'b0011011), .eq(Frase_Detectada));  // open: gt, lt
  ROM #(.addrWidth(7), .dataWidth(7)) rom_1 (.addr(counter_1_q), .data(rom_1_data));  // open: sel
  Comparator #(.width(7)) comparator_2 (.a(rom_1_data), .b(Char_In), .eq(comparator_2_eq));  // open: gt, lt
  not not_1 (not_1_out, comparator_2_eq);
  not not_2 (not_2_out, comparator_3_eq);
  Comparator #(.width(7)) comparator_3 (.a(Char_In), .b({7{1'b0}}), .eq(comparator_3_eq));  // open: gt, lt

  // Notes on the sheet:
  //   contents of rom_1 (hex, n*v repeats v):
  //   51 75 61 6c 20 61 20 73 75 61 20 73 65 72 69 65 20 66 61 76 6f 72 69 74 61 3f a
endmodule

// R10
module Resposta_10 (
  input  Iniciar,
  input  Clock,
  output Falando,
  output [6:0] Char_Out
);

  wire comparator_1_eq;
  wire [6:0] counter_1_q, rom_1_data;

  D_Flip_Flop d_ff_1 (.clk(Clock), .Q(Falando), .preset(Iniciar), .reset(comparator_1_eq));  // open: D, Qn, en
  Counter #(.width(7), .max('h7f)) counter_1 (
    .count(Falando), .Q(counter_1_q), .clk(Clock), .clr(comparator_1_eq));  // open: load, D, carry
  Comparator #(.width(7)) comparator_1 (.a(counter_1_q), .b(7'b0010100), .eq(comparator_1_eq));  // open: gt, lt
  ROM #(.addrWidth(7), .dataWidth(7)) rom_1 (.addr(counter_1_q), .data(rom_1_data));  // open: sel
  assign Char_Out = Falando ? rom_1_data : 7'bz;  // Controlled_Buffer controlled_buffer_1

  // Notes on the sheet:
  //   contents of rom_1 (hex, n*v repeats v):
  //   59 4f 55 20 41 52 45 20 48 45 49 53 45 4e 42 45 52 47 21 a
endmodule

// D10
module Detector_10 (
  input  [6:0] Char_In,
  input  Clock,
  input  Reset_Externo,
  output Frase_Detectada
);

  wire and_1_out, comparator_2_eq, comparator_3_eq, not_1_out, not_2_out, or_1_out;
  wire [6:0] counter_1_q, rom_1_data;

  Counter #(.width(7), .max('h7f)) counter_1 (
    .count(not_2_out), .Q(counter_1_q), .clk(Clock), .clr(or_1_out));  // open: load, D, carry
  or or_1 (or_1_out, Reset_Externo, and_1_out, Frase_Detectada);
  and and_1 (and_1_out, not_1_out, not_2_out);
  Comparator #(.width(7)) comparator_1 (.a(counter_1_q), .b(7'b0001100), .eq(Frase_Detectada));  // open: gt, lt
  ROM #(.addrWidth(7), .dataWidth(7)) rom_1 (.addr(counter_1_q), .data(rom_1_data));  // open: sel
  Comparator #(.width(7)) comparator_2 (.a(rom_1_data), .b(Char_In), .eq(comparator_2_eq));  // open: gt, lt
  not not_1 (not_1_out, comparator_2_eq);
  not not_2 (not_2_out, comparator_3_eq);
  Comparator #(.width(7)) comparator_3 (.a(Char_In), .b({7{1'b0}}), .eq(comparator_3_eq));  // open: gt, lt

  // Notes on the sheet:
  //   contents of rom_1 (hex, n*v repeats v):
  //   53 61 79 20 6d 79 20 6e 61 6d 65 a
endmodule

// R11
module Resposta_11 (
  input  Iniciar,
  input  Clock,
  output Falando,
  output [6:0] Char_Out
);

  wire comparator_1_eq;
  wire [6:0] counter_1_q, rom_1_data;

  D_Flip_Flop d_ff_1 (.clk(Clock), .Q(Falando), .preset(Iniciar), .reset(comparator_1_eq));  // open: D, Qn, en
  Counter #(.width(7), .max('h7f)) counter_1 (
    .count(Falando), .Q(counter_1_q), .clk(Clock), .clr(comparator_1_eq));  // open: load, D, carry
  Comparator #(.width(7)) comparator_1 (.a(counter_1_q), .b(7'b0100100), .eq(comparator_1_eq));  // open: gt, lt
  ROM #(.addrWidth(7), .dataWidth(7)) rom_1 (.addr(counter_1_q), .data(rom_1_data));  // open: sel
  assign Char_Out = Falando ? rom_1_data : 7'bz;  // Controlled_Buffer controlled_buffer_1

  // Notes on the sheet:
  //   contents of rom_1 (hex, n*v repeats v):
  //   4f 20 71 75 65 20 6f 20 5a 65 72 6f 20 66 61 6c 6f 75 20 70 61 72 61 20 6f 20 55 6d 3f a 4e 61 64 61
  //   2e a
endmodule

// D11
module Detector_11 (
  input  [6:0] Char_In,
  input  Clock,
  input  Reset_Externo,
  output Frase_Detectada
);

  wire and_1_out, comparator_2_eq, comparator_3_eq, not_1_out, not_2_out, or_1_out;
  wire [6:0] counter_1_q, rom_1_data;

  Counter #(.width(7), .max('h7f)) counter_1 (
    .count(not_2_out), .Q(counter_1_q), .clk(Clock), .clr(or_1_out));  // open: load, D, carry
  or or_1 (or_1_out, Reset_Externo, and_1_out, Frase_Detectada);
  and and_1 (and_1_out, not_1_out, not_2_out);
  Comparator #(.width(7)) comparator_1 (.a(counter_1_q), .b(7'b0010000), .eq(Frase_Detectada));  // open: gt, lt
  ROM #(.addrWidth(7), .dataWidth(7)) rom_1 (.addr(counter_1_q), .data(rom_1_data));  // open: sel
  not not_1 (not_1_out, comparator_2_eq);
  Comparator #(.width(7)) comparator_2 (.a(rom_1_data), .b(Char_In), .eq(comparator_2_eq));  // open: gt, lt
  Comparator #(.width(7)) comparator_3 (.a(Char_In), .b({7{1'b0}}), .eq(comparator_3_eq));  // open: gt, lt
  not not_2 (not_2_out, comparator_3_eq);

  // Notes on the sheet:
  //   contents of rom_1 (hex, n*v repeats v):
  //   43 6f 6e 74 65 20 75 6d 61 20 70 69 61 64 61 a
endmodule

// R12
module Resposta_12 (
  input  Iniciar,
  input  Clock,
  output Falando,
  output [6:0] Char_Out
);

  wire comparator_1_eq;
  wire [6:0] counter_1_q, rom_1_data;

  D_Flip_Flop d_ff_1 (.clk(Clock), .Q(Falando), .preset(Iniciar), .reset(comparator_1_eq));  // open: D, Qn, en
  Counter #(.width(7), .max('h7f)) counter_1 (
    .count(Falando), .Q(counter_1_q), .clk(Clock), .clr(comparator_1_eq));  // open: load, D, carry
  Comparator #(.width(7)) comparator_1 (.a(counter_1_q), .b(7'b0101000), .eq(comparator_1_eq));  // open: gt, lt
  ROM #(.addrWidth(7), .dataWidth(7)) rom_1 (.addr(counter_1_q), .data(rom_1_data));  // open: sel
  assign Char_Out = Falando ? rom_1_data : 7'bz;  // Controlled_Buffer controlled_buffer_1

  // Notes on the sheet:
  //   contents of rom_1 (hex, n*v repeats v):
  //   45 20 68 6f 72 61 20 64 65 20 6d 6f 6e 74 61 72 20 63 69 72 63 75 69 74 6f 73 20 65 6c 65 74 72 6f
  //   6e 69 63 6f 73 21 a
endmodule

// D12
module Detector_12 (
  input  [6:0] Char_In,
  input  Clock,
  input  Reset_Externo,
  output Frase_Detectada
);

  wire and_1_out, comparator_2_eq, comparator_3_eq, not_1_out, not_2_out, or_1_out;
  wire [6:0] counter_1_q, rom_1_data;

  Counter #(.width(7), .max('h7f)) counter_1 (
    .count(not_2_out), .Q(counter_1_q), .clk(Clock), .clr(or_1_out));  // open: load, D, carry
  or or_1 (or_1_out, Reset_Externo, and_1_out, Frase_Detectada);
  and and_1 (and_1_out, not_1_out, not_2_out);
  Comparator #(.width(7)) comparator_1 (.a(counter_1_q), .b(7'b0001111), .eq(Frase_Detectada));  // open: gt, lt
  ROM #(.addrWidth(7), .dataWidth(7)) rom_1 (.addr(counter_1_q), .data(rom_1_data));  // open: sel
  not not_1 (not_1_out, comparator_2_eq);
  Comparator #(.width(7)) comparator_2 (.a(rom_1_data), .b(Char_In), .eq(comparator_2_eq));  // open: gt, lt
  not not_2 (not_2_out, comparator_3_eq);
  Comparator #(.width(7)) comparator_3 (.a(Char_In), .b({7{1'b0}}), .eq(comparator_3_eq));  // open: gt, lt

  // Notes on the sheet:
  //   contents of rom_1 (hex, n*v repeats v):
  //   51 75 65 20 68 6f 72 61 73 20 73 61 6f 3f a
endmodule

// R13
module Resposta_13 (
  input  Iniciar,
  input  Clock,
  output Falando,
  output [6:0] Char_Out
);

  wire comparator_1_eq;
  wire [6:0] counter_1_q, rom_1_data;

  D_Flip_Flop d_ff_1 (.clk(Clock), .Q(Falando), .preset(Iniciar), .reset(comparator_1_eq));  // open: D, Qn, en
  Counter #(.width(7), .max('h7f)) counter_1 (
    .count(Falando), .Q(counter_1_q), .clk(Clock), .clr(comparator_1_eq));  // open: load, D, carry
  Comparator #(.width(7)) comparator_1 (.a(counter_1_q), .b(7'b0110110), .eq(comparator_1_eq));  // open: gt, lt
  ROM #(.addrWidth(7), .dataWidth(7)) rom_1 (.addr(counter_1_q), .data(rom_1_data));  // open: sel
  assign Char_Out = Falando ? rom_1_data : 7'bz;  // Controlled_Buffer controlled_buffer_1

  // Notes on the sheet:
  //   contents of rom_1 (hex, n*v repeats v):
  //   53 65 6d 20 64 75 76 69 64 61 73 20 50 65 6c 65 2c 20 6f 20 6d 61 69 6f 72 20 6a 6f 67 61 64 6f 72
  //   20 64 65 20 74 6f 64 6f 73 20 6f 73 20 74 65 6d 70 6f 73 21 a
endmodule

// D13
module Detector_13 (
  input  [6:0] Char_In,
  input  Clock,
  input  Reset_Externo,
  output Frase_Detectada
);

  wire and_1_out, comparator_2_eq, comparator_3_eq, not_1_out, not_2_out, or_1_out;
  wire [6:0] counter_1_q, rom_1_data;

  Counter #(.width(7), .max('h7f)) counter_1 (
    .count(not_2_out), .Q(counter_1_q), .clk(Clock), .clr(or_1_out));  // open: load, D, carry
  or or_1 (or_1_out, Reset_Externo, and_1_out, Frase_Detectada);
  and and_1 (and_1_out, not_1_out, not_2_out);
  Comparator #(.width(7)) comparator_1 (.a(counter_1_q), .b(7'b0010010), .eq(Frase_Detectada));  // open: gt, lt
  ROM #(.addrWidth(7), .dataWidth(7)) rom_1 (.addr(counter_1_q), .data(rom_1_data));  // open: sel
  not not_1 (not_1_out, comparator_2_eq);
  Comparator #(.width(7)) comparator_2 (.a(rom_1_data), .b(Char_In), .eq(comparator_2_eq));  // open: gt, lt
  not not_2 (not_2_out, comparator_3_eq);
  Comparator #(.width(7)) comparator_3 (.a(Char_In), .b({7{1'b0}}), .eq(comparator_3_eq));  // open: gt, lt

  // Notes on the sheet:
  //   contents of rom_1 (hex, n*v repeats v):
  //   50 65 6c 65 20 6f 75 20 4d 61 72 61 64 6f 6e 61 3f a
endmodule

// R14
module Resposta_14 (
  input  Iniciar,
  input  Clock,
  output Falando,
  output [6:0] Char_Out
);

  wire comparator_1_eq;
  wire [6:0] counter_1_q, rom_1_data;

  D_Flip_Flop d_ff_1 (.clk(Clock), .Q(Falando), .preset(Iniciar), .reset(comparator_1_eq));  // open: D, Qn, en
  Counter #(.width(7), .max('h7f)) counter_1 (
    .count(Falando), .Q(counter_1_q), .clk(Clock), .clr(comparator_1_eq));  // open: load, D, carry
  Comparator #(.width(7)) comparator_1 (.a(counter_1_q), .b(7'b0010101), .eq(comparator_1_eq));  // open: gt, lt
  ROM #(.addrWidth(7), .dataWidth(7)) rom_1 (.addr(counter_1_q), .data(rom_1_data));  // open: sel
  assign Char_Out = Falando ? rom_1_data : 7'bz;  // Controlled_Buffer controlled_buffer_1

  // Notes on the sheet:
  //   contents of rom_1 (hex, n*v repeats v):
  //   45 75 20 70 72 65 66 69 72 6f 20 61 20 4d 61 72 76 65 6c 21 a
endmodule

// D14
module Detector_14 (
  input  [6:0] Char_In,
  input  Clock,
  input  Reset_Externo,
  output Frase_Detectada
);

  wire and_1_out, comparator_2_eq, comparator_3_eq, not_1_out, not_2_out, or_1_out;
  wire [6:0] counter_1_q, rom_1_data;

  Counter #(.width(7), .max('h7f)) counter_1 (
    .count(not_2_out), .Q(counter_1_q), .clk(Clock), .clr(or_1_out));  // open: load, D, carry
  or or_1 (or_1_out, Reset_Externo, and_1_out, Frase_Detectada);
  and and_1 (and_1_out, not_1_out, not_2_out);
  Comparator #(.width(7)) comparator_1 (.a(counter_1_q), .b(7'b0001110), .eq(Frase_Detectada));  // open: gt, lt
  ROM #(.addrWidth(7), .dataWidth(7)) rom_1 (.addr(counter_1_q), .data(rom_1_data));  // open: sel
  not not_1 (not_1_out, comparator_2_eq);
  Comparator #(.width(7)) comparator_2 (.a(rom_1_data), .b(Char_In), .eq(comparator_2_eq));  // open: gt, lt
  not not_2 (not_2_out, comparator_3_eq);
  Comparator #(.width(7)) comparator_3 (.a(Char_In), .b({7{1'b0}}), .eq(comparator_3_eq));  // open: gt, lt

  // Notes on the sheet:
  //   contents of rom_1 (hex, n*v repeats v):
  //   4d 61 72 76 65 6c 20 6f 75 20 44 43 3f a
endmodule

// R15
module Resposta_15 (
  input  Iniciar,
  input  Clock,
  output Falando,
  output [6:0] Char_Out
);

  wire comparator_1_eq;
  wire [6:0] counter_1_q, rom_1_data;

  D_Flip_Flop d_ff_1 (.clk(Clock), .Q(Falando), .preset(Iniciar), .reset(comparator_1_eq));  // open: D, Qn, en
  Counter #(.width(7), .max('h7f)) counter_1 (
    .count(Falando), .Q(counter_1_q), .clk(Clock), .clr(comparator_1_eq));  // open: load, D, carry
  Comparator #(.width(7)) comparator_1 (.a(counter_1_q), .b(7'b1001101), .eq(comparator_1_eq));  // open: gt, lt
  ROM #(.addrWidth(7), .dataWidth(7)) rom_1 (.addr(counter_1_q), .data(rom_1_data));  // open: sel
  assign Char_Out = Falando ? rom_1_data : 7'bz;  // Controlled_Buffer controlled_buffer_1

  // Notes on the sheet:
  //   contents of rom_1 (hex, n*v repeats v):
  //   43 69 6d 61 2c 20 43 69 6d 61 2c 20 42 61 69 78 6f 2c 20 42 61 69 78 6f 2c 20 45 73 71 75 65 72 64
  //   61 2c 20 44 69 72 65 69 74 61 2c 20 45 73 71 75 65 72 64 61 2c 20 44 69 72 65 69 74 61 2c 20 42 2c
  //   20 41 2c 20 53 74 61 72 74 21 a
endmodule

// D15
module Detector_15 (
  input  [6:0] Char_In,
  input  Clock,
  input  Reset_Externo,
  output Frase_Detectada
);

  wire and_1_out, comparator_2_eq, comparator_3_eq, not_1_out, not_2_out, or_1_out;
  wire [6:0] counter_1_q, rom_1_data;

  Counter #(.width(7), .max('h7f)) counter_1 (
    .count(not_2_out), .Q(counter_1_q), .clk(Clock), .clr(or_1_out));  // open: load, D, carry
  or or_1 (or_1_out, Reset_Externo, and_1_out, Frase_Detectada);
  and and_1 (and_1_out, not_1_out, not_2_out);
  Comparator #(.width(7)) comparator_1 (.a(counter_1_q), .b(7'b0001100), .eq(Frase_Detectada));  // open: gt, lt
  ROM #(.addrWidth(7), .dataWidth(7)) rom_1 (.addr(counter_1_q), .data(rom_1_data));  // open: sel
  not not_1 (not_1_out, comparator_2_eq);
  Comparator #(.width(7)) comparator_2 (.a(rom_1_data), .b(Char_In), .eq(comparator_2_eq));  // open: gt, lt
  Comparator #(.width(7)) comparator_3 (.a(Char_In), .b({7{1'b0}}), .eq(comparator_3_eq));  // open: gt, lt
  not not_2 (not_2_out, comparator_3_eq);

  // Notes on the sheet:
  //   contents of rom_1 (hex, n*v repeats v):
  //   4b 6f 6e 61 6d 69 20 63 6f 64 65 a
endmodule

// R16
module Resposta_16 (
  input  Iniciar,
  input  Clock,
  output Falando,
  output [6:0] Char_Out
);

  wire comparator_1_eq;
  wire [6:0] counter_1_q, rom_1_data;

  D_Flip_Flop d_ff_1 (.clk(Clock), .Q(Falando), .preset(Iniciar), .reset(comparator_1_eq));  // open: D, Qn, en
  Counter #(.width(7), .max('h7f)) counter_1 (
    .count(Falando), .Q(counter_1_q), .clk(Clock), .clr(comparator_1_eq));  // open: load, D, carry
  Comparator #(.width(7)) comparator_1 (.a(counter_1_q), .b(7'b0100100), .eq(comparator_1_eq));  // open: gt, lt
  ROM #(.addrWidth(7), .dataWidth(7)) rom_1 (.addr(counter_1_q), .data(rom_1_data));  // open: sel
  assign Char_Out = Falando ? rom_1_data : 7'bz;  // Controlled_Buffer controlled_buffer_1

  // Notes on the sheet:
  //   contents of rom_1 (hex, n*v repeats v):
  //   45 75 20 73 6f 75 20 75 6d 61 20 49 6e 74 65 6c 69 67 65 6e 63 69 61 20 41 72 74 69 66 69 63 69 61
  //   6c 21 a
endmodule

// D16
module Detector_16 (
  input  [6:0] Char_In,
  input  Clock,
  input  Reset_Externo,
  output Frase_Detectada
);

  wire and_1_out, comparator_2_eq, comparator_3_eq, not_1_out, not_2_out, or_1_out;
  wire [6:0] counter_1_q, rom_1_data;

  Counter #(.width(7), .max('h7f)) counter_1 (
    .count(not_2_out), .Q(counter_1_q), .clk(Clock), .clr(or_1_out));  // open: load, D, carry
  or or_1 (or_1_out, Reset_Externo, and_1_out, Frase_Detectada);
  and and_1 (and_1_out, not_1_out, not_2_out);
  Comparator #(.width(7)) comparator_1 (.a(counter_1_q), .b(7'b0010010), .eq(Frase_Detectada));  // open: gt, lt
  ROM #(.addrWidth(7), .dataWidth(7)) rom_1 (.addr(counter_1_q), .data(rom_1_data));  // open: sel
  Comparator #(.width(7)) comparator_2 (.a(rom_1_data), .b(Char_In), .eq(comparator_2_eq));  // open: gt, lt
  not not_1 (not_1_out, comparator_2_eq);
  not not_2 (not_2_out, comparator_3_eq);
  Comparator #(.width(7)) comparator_3 (.a(Char_In), .b({7{1'b0}}), .eq(comparator_3_eq));  // open: gt, lt

  // Notes on the sheet:
  //   contents of rom_1 (hex, n*v repeats v):
  //   43 6f 6e 74 65 20 75 6d 61 20 6d 65 6e 74 69 72 61 a
endmodule

// R17
module Resposta_17 (
  input  Iniciar,
  input  Clock,
  output Falando,
  output [6:0] Char_Out
);

  wire comparator_1_eq;
  wire [6:0] counter_1_q, rom_1_data;

  D_Flip_Flop d_ff_1 (.clk(Clock), .Q(Falando), .preset(Iniciar), .reset(comparator_1_eq));  // open: D, Qn, en
  Counter #(.width(7), .max('h7f)) counter_1 (
    .count(Falando), .Q(counter_1_q), .clk(Clock), .clr(comparator_1_eq));  // open: load, D, carry
  Comparator #(.width(7)) comparator_1 (.a(counter_1_q), .b(7'b0001010), .eq(comparator_1_eq));  // open: gt, lt
  ROM #(.addrWidth(7), .dataWidth(7)) rom_1 (.addr(counter_1_q), .data(rom_1_data));  // open: sel
  assign Char_Out = Falando ? rom_1_data : 7'bz;  // Controlled_Buffer controlled_buffer_1

  // Notes on the sheet:
  //   contents of rom_1 (hex, n*v repeats v):
  //   50 43 20 47 61 6d 65 72 21 a
endmodule

// D17
module Detector_17 (
  input  [6:0] Char_In,
  input  Clock,
  input  Reset_Externo,
  output Frase_Detectada
);

  wire and_1_out, comparator_2_eq, comparator_3_eq, not_1_out, not_2_out, or_1_out;
  wire [6:0] counter_1_q, rom_1_data;

  Counter #(.width(7), .max('h7f)) counter_1 (
    .count(not_2_out), .Q(counter_1_q), .clk(Clock), .clr(or_1_out));  // open: load, D, carry
  or or_1 (or_1_out, Reset_Externo, and_1_out, Frase_Detectada);
  and and_1 (and_1_out, not_1_out, not_2_out);
  Comparator #(.width(7)) comparator_1 (.a(counter_1_q), .b(7'b0010101), .eq(Frase_Detectada));  // open: gt, lt
  ROM #(.addrWidth(7), .dataWidth(7)) rom_1 (.addr(counter_1_q), .data(rom_1_data));  // open: sel
  not not_1 (not_1_out, comparator_2_eq);
  Comparator #(.width(7)) comparator_2 (.a(rom_1_data), .b(Char_In), .eq(comparator_2_eq));  // open: gt, lt
  not not_2 (not_2_out, comparator_3_eq);
  Comparator #(.width(7)) comparator_3 (.a(Char_In), .b({7{1'b0}}), .eq(comparator_3_eq));  // open: gt, lt

  // Notes on the sheet:
  //   contents of rom_1 (hex, n*v repeats v):
  //   50 6c 61 79 73 74 61 74 69 6f 6e 20 6f 75 20 58 62 6f 78 3f a
endmodule

// R18
module Resposta_18 (
  input  Iniciar,
  input  Clock,
  output Falando,
  output [6:0] Char_Out
);

  wire comparator_1_eq;
  wire [6:0] counter_1_q, rom_1_data;

  D_Flip_Flop d_ff_1 (.clk(Clock), .Q(Falando), .preset(Iniciar), .reset(comparator_1_eq));  // open: D, Qn, en
  Counter #(.width(7), .max('h7f)) counter_1 (
    .count(Falando), .Q(counter_1_q), .clk(Clock), .clr(comparator_1_eq));  // open: load, D, carry
  Comparator #(.width(7)) comparator_1 (.a(counter_1_q), .b(7'b0100101), .eq(comparator_1_eq));  // open: gt, lt
  ROM #(.addrWidth(7), .dataWidth(7)) rom_1 (.addr(counter_1_q), .data(rom_1_data));  // open: sel
  assign Char_Out = Falando ? rom_1_data : 7'bz;  // Controlled_Buffer controlled_buffer_1

  // Notes on the sheet:
  //   contents of rom_1 (hex, n*v repeats v):
  //   45 75 20 6e 61 6f 20 76 6f 75 20 64 6f 6d 69 6e 61 72 20 6f 20 6d 75 6e 64 6f 21 20 41 69 6e 64 61
  //   2e 2e 2e a
endmodule

// D18
module Detector_18 (
  input  [6:0] Char_In,
  input  Clock,
  input  Reset_Externo,
  output Frase_Detectada
);

  wire and_1_out, comparator_2_eq, comparator_3_eq, not_1_out, not_2_out, or_1_out;
  wire [6:0] counter_1_q, rom_1_data;

  Counter #(.width(7), .max('h7f)) counter_1 (
    .count(not_2_out), .Q(counter_1_q), .clk(Clock), .clr(or_1_out));  // open: load, D, carry
  or or_1 (or_1_out, Reset_Externo, and_1_out, Frase_Detectada);
  and and_1 (and_1_out, not_1_out, not_2_out);
  Comparator #(.width(7)) comparator_1 (.a(counter_1_q), .b(7'b0011010), .eq(Frase_Detectada));  // open: gt, lt
  ROM #(.addrWidth(7), .dataWidth(7)) rom_1 (.addr(counter_1_q), .data(rom_1_data));  // open: sel
  not not_1 (not_1_out, comparator_2_eq);
  Comparator #(.width(7)) comparator_2 (.a(rom_1_data), .b(Char_In), .eq(comparator_2_eq));  // open: gt, lt
  Comparator #(.width(7)) comparator_3 (.a(Char_In), .b({7{1'b0}}), .eq(comparator_3_eq));  // open: gt, lt
  not not_2 (not_2_out, comparator_3_eq);

  // Notes on the sheet:
  //   contents of rom_1 (hex, n*v repeats v):
  //   56 6f 63 65 20 76 61 69 20 64 6f 6d 69 6e 61 72 20 6f 20 6d 75 6e 64 6f 3f a
endmodule

// R19
module Resposta_19 (
  input  Iniciar,
  input  Clock,
  output Falando,
  output [6:0] Char_Out
);

  wire comparator_1_eq;
  wire [6:0] counter_1_q, rom_1_data;

  D_Flip_Flop d_ff_1 (.clk(Clock), .Q(Falando), .preset(Iniciar), .reset(comparator_1_eq));  // open: D, Qn, en
  Counter #(.width(7), .max('h7f)) counter_1 (
    .count(Falando), .Q(counter_1_q), .clk(Clock), .clr(comparator_1_eq));  // open: load, D, carry
  Comparator #(.width(7)) comparator_1 (.a(counter_1_q), .b(7'b0100011), .eq(comparator_1_eq));  // open: gt, lt
  ROM #(.addrWidth(7), .dataWidth(7)) rom_1 (.addr(counter_1_q), .data(rom_1_data));  // open: sel
  assign Char_Out = Falando ? rom_1_data : 7'bz;  // Controlled_Buffer controlled_buffer_1

  // Notes on the sheet:
  //   contents of rom_1 (hex, n*v repeats v):
  //   4d 69 6e 68 61 20 62 61 6e 64 61 20 66 61 76 6f 72 69 74 61 20 65 20 50 69 6e 6b 20 46 6c 6f 79 64
  //   21 a
endmodule

// D19
module Detector_19 (
  input  [6:0] Char_In,
  input  Clock,
  input  Reset_Externo,
  output Frase_Detectada
);

  wire and_1_out, comparator_2_eq, comparator_3_eq, not_1_out, not_2_out, or_1_out;
  wire [6:0] counter_1_q, rom_1_data;

  Counter #(.width(7), .max('h7f)) counter_1 (
    .count(not_2_out), .Q(counter_1_q), .clk(Clock), .clr(or_1_out));  // open: load, D, carry
  or or_1 (or_1_out, Reset_Externo, and_1_out, Frase_Detectada);
  and and_1 (and_1_out, not_1_out, not_2_out);
  Comparator #(.width(7)) comparator_1 (.a(counter_1_q), .b(7'b0011001), .eq(Frase_Detectada));  // open: gt, lt
  ROM #(.addrWidth(7), .dataWidth(7)) rom_1 (.addr(counter_1_q), .data(rom_1_data));  // open: sel
  Comparator #(.width(7)) comparator_2 (.a(rom_1_data), .b(Char_In), .eq(comparator_2_eq));  // open: gt, lt
  not not_1 (not_1_out, comparator_2_eq);
  Comparator #(.width(7)) comparator_3 (.a(Char_In), .b({7{1'b0}}), .eq(comparator_3_eq));  // open: gt, lt
  not not_2 (not_2_out, comparator_3_eq);

  // Notes on the sheet:
  //   contents of rom_1 (hex, n*v repeats v):
  //   51 75 61 6c 20 73 75 61 20 62 61 6e 64 61 20 66 61 76 6f 72 69 74 61 3f a
endmodule

// R20
module Resposta_20 (
  input  Iniciar,
  input  Clock,
  output Falando,
  output [6:0] Char_Out
);

  wire comparator_1_eq;
  wire [6:0] counter_1_q, rom_1_data;

  D_Flip_Flop d_ff_1 (.clk(Clock), .Q(Falando), .preset(Iniciar), .reset(comparator_1_eq));  // open: D, Qn, en
  Counter #(.width(7), .max('h7f)) counter_1 (
    .count(Falando), .Q(counter_1_q), .clk(Clock), .clr(comparator_1_eq));  // open: load, D, carry
  Comparator #(.width(7)) comparator_1 (.a(counter_1_q), .b(7'b1010000), .eq(comparator_1_eq));  // open: gt, lt
  ROM #(.addrWidth(7), .dataWidth(7)) rom_1 (.addr(counter_1_q), .data(rom_1_data));  // open: sel
  assign Char_Out = Falando ? rom_1_data : 7'bz;  // Controlled_Buffer controlled_buffer_1

  // Notes on the sheet:
  //   contents of rom_1 (hex, n*v repeats v):
  //   50 61 72 61 62 65 6e 73 20 70 72 61 20 76 6f 63 65 2c 20 6e 65 73 73 61 20 64 61 74 61 20 71 75 65
  //   72 69 64 61 2c 20 6d 75 69 74 61 73 20 66 65 6c 69 63 69 64 61 64 65 73 2c 20 6d 75 69 74 6f 73 20
  //   61 6e 6f 73 20 64 65 20 76 69 64 61 21 a
endmodule

// D20
module Detector_20 (
  input  [6:0] Char_In,
  input  Clock,
  input  Reset_Externo,
  output Frase_Detectada
);

  wire and_1_out, comparator_2_eq, comparator_3_eq, not_1_out, not_2_out, or_1_out;
  wire [6:0] counter_1_q, rom_1_data;

  Counter #(.width(7), .max('h7f)) counter_1 (
    .count(not_2_out), .Q(counter_1_q), .clk(Clock), .clr(or_1_out));  // open: load, D, carry
  or or_1 (or_1_out, Reset_Externo, and_1_out, Frase_Detectada);
  and and_1 (and_1_out, not_1_out, not_2_out);
  Comparator #(.width(7)) comparator_1 (.a(counter_1_q), .b(7'b0001100), .eq(Frase_Detectada));  // open: gt, lt
  ROM #(.addrWidth(7), .dataWidth(7)) rom_1 (.addr(counter_1_q), .data(rom_1_data));  // open: sel
  Comparator #(.width(7)) comparator_2 (.a(rom_1_data), .b(Char_In), .eq(comparator_2_eq));  // open: gt, lt
  not not_1 (not_1_out, comparator_2_eq);
  Comparator #(.width(7)) comparator_3 (.a(Char_In), .b({7{1'b0}}), .eq(comparator_3_eq));  // open: gt, lt
  not not_2 (not_2_out, comparator_3_eq);

  // Notes on the sheet:
  //   contents of rom_1 (hex, n*v repeats v):
  //   41 6e 69 76 65 72 73 61 72 69 6f a
endmodule

// R21
module Resposta_21 (
  input  Iniciar,
  input  Clock,
  output Falando,
  output [6:0] Char_Out
);

  wire comparator_1_eq;
  wire [6:0] counter_1_q, rom_1_data;

  D_Flip_Flop d_ff_1 (.clk(Clock), .Q(Falando), .preset(Iniciar), .reset(comparator_1_eq));  // open: D, Qn, en
  Counter #(.width(7), .max('h7f)) counter_1 (
    .count(Falando), .Q(counter_1_q), .clk(Clock), .clr(comparator_1_eq));  // open: load, D, carry
  Comparator #(.width(7)) comparator_1 (.a(counter_1_q), .b(7'b1110011), .eq(comparator_1_eq));  // open: gt, lt
  ROM #(.addrWidth(7), .dataWidth(7)) rom_1 (.addr(counter_1_q), .data(rom_1_data));  // open: sel
  assign Char_Out = Falando ? rom_1_data : 7'bz;  // Controlled_Buffer controlled_buffer_1

  // Notes on the sheet:
  //   contents of rom_1 (hex, n*v repeats v):
  //   4d 65 75 73 20 63 72 69 61 64 6f 72 65 73 20 73 61 6f 3a 20 41 72 74 68 75 72 20 44 65 73 74 72 6f
  //   2c 20 47 75 73 74 61 76 6f 20 4d 61 75 72 69 7a 2c 20 47 75 73 74 61 76 6f 20 5a 61 63 63 68 65 75
  //   2c 20 53 61 6d 61 72 20 56 69 63 74 6f 72 2c 20 56 69 6e 69 63 69 75 73 20 53 74 72 61 7a 7a 61 20
  //   65 20 56 69 74 6f 72 20 42 61 72 62 6f 73 61 a
endmodule

// D21
module Detector_21 (
  input  [6:0] Char_In,
  input  Clock,
  input  Reset_Externo,
  output Frase_Detectada
);

  wire and_1_out, comparator_2_eq, comparator_3_eq, not_1_out, not_2_out, or_1_out;
  wire [6:0] counter_1_q, rom_1_data;

  Counter #(.width(7), .max('h7f)) counter_1 (
    .count(not_2_out), .Q(counter_1_q), .clk(Clock), .clr(or_1_out));  // open: load, D, carry
  or or_1 (or_1_out, Reset_Externo, and_1_out, Frase_Detectada);
  and and_1 (and_1_out, not_1_out, not_2_out);
  Comparator #(.width(7)) comparator_1 (.a(counter_1_q), .b(7'b0000110), .eq(Frase_Detectada));  // open: gt, lt
  ROM #(.addrWidth(7), .dataWidth(7)) rom_1 (.addr(counter_1_q), .data(rom_1_data));  // open: sel
  Comparator #(.width(7)) comparator_2 (.a(rom_1_data), .b(Char_In), .eq(comparator_2_eq));  // open: gt, lt
  not not_1 (not_1_out, comparator_2_eq);
  Comparator #(.width(7)) comparator_3 (.a(Char_In), .b({7{1'b0}}), .eq(comparator_3_eq));  // open: gt, lt
  not not_2 (not_2_out, comparator_3_eq);

  // Notes on the sheet:
  //   contents of rom_1 (hex, n*v repeats v):
  //   47 72 75 70 6f a
endmodule

// R22
module Resposta_22 (
  input  Iniciar,
  input  Clock,
  output Falando,
  output [6:0] Char_Out
);

  wire comparator_1_eq;
  wire [6:0] counter_1_q, rom_1_data;

  D_Flip_Flop d_ff_1 (.clk(Clock), .Q(Falando), .preset(Iniciar), .reset(comparator_1_eq));  // open: D, Qn, en
  Counter #(.width(7), .max('h7f)) counter_1 (
    .count(Falando), .Q(counter_1_q), .clk(Clock), .clr(comparator_1_eq));  // open: load, D, carry
  Comparator #(.width(7)) comparator_1 (.a(counter_1_q), .b(7'b0100111), .eq(comparator_1_eq));  // open: gt, lt
  ROM #(.addrWidth(7), .dataWidth(7)) rom_1 (.addr(counter_1_q), .data(rom_1_data));  // open: sel
  assign Char_Out = Falando ? rom_1_data : 7'bz;  // Controlled_Buffer controlled_buffer_1

  // Notes on the sheet:
  //   contents of rom_1 (hex, n*v repeats v):
  //   4d 69 6e 68 61 20 70 65 73 73 6f 61 20 66 61 76 6f 72 69 74 61 20 65 20 6f 20 41 6c 61 6e 20 54 75
  //   72 69 6e 67 21 a
endmodule

// D22
module Detector_22 (
  input  [6:0] Char_In,
  input  Clock,
  input  Reset_Externo,
  output Frase_Detectada
);

  wire and_1_out, comparator_2_eq, comparator_3_eq, not_1_out, not_2_out, or_1_out;
  wire [6:0] counter_1_q, rom_1_data;

  Counter #(.width(7), .max('h7f)) counter_1 (
    .count(not_2_out), .Q(counter_1_q), .clk(Clock), .clr(or_1_out));  // open: load, D, carry
  or or_1 (or_1_out, Reset_Externo, and_1_out, Frase_Detectada);
  and and_1 (and_1_out, not_1_out, not_2_out);
  Comparator #(.width(7)) comparator_1 (.a(counter_1_q), .b(7'b0010010), .eq(Frase_Detectada));  // open: gt, lt
  ROM #(.addrWidth(7), .dataWidth(7)) rom_1 (.addr(counter_1_q), .data(rom_1_data));  // open: sel
  Comparator #(.width(7)) comparator_2 (.a(rom_1_data), .b(Char_In), .eq(comparator_2_eq));  // open: gt, lt
  not not_1 (not_1_out, comparator_2_eq);
  not not_2 (not_2_out, comparator_3_eq);
  Comparator #(.width(7)) comparator_3 (.a(Char_In), .b({7{1'b0}}), .eq(comparator_3_eq));  // open: gt, lt

  // Notes on the sheet:
  //   contents of rom_1 (hex, n*v repeats v):
  //   51 75 65 6d 20 65 20 73 65 75 20 69 64 6f 6c 6f 3f a
endmodule

// R23
module Resposta_23 (
  input  Iniciar,
  input  Clock,
  output Falando,
  output [6:0] Char_Out
);

  wire comparator_1_eq;
  wire [6:0] counter_1_q, rom_1_data;

  D_Flip_Flop d_ff_1 (.clk(Clock), .Q(Falando), .preset(Iniciar), .reset(comparator_1_eq));  // open: D, Qn, en
  Counter #(.width(7), .max('h7f)) counter_1 (
    .count(Falando), .Q(counter_1_q), .clk(Clock), .clr(comparator_1_eq));  // open: load, D, carry
  Comparator #(.width(7)) comparator_1 (.a(counter_1_q), .b(7'b0101011), .eq(comparator_1_eq));  // open: gt, lt
  ROM #(.addrWidth(7), .dataWidth(7)) rom_1 (.addr(counter_1_q), .data(rom_1_data));  // open: sel
  assign Char_Out = Falando ? rom_1_data : 7'bz;  // Controlled_Buffer controlled_buffer_1

  // Notes on the sheet:
  //   contents of rom_1 (hex, n*v repeats v):
  //   53 69 6d 2c 20 6d 65 75 73 20 66 69 6c 68 6f 73 20 73 61 6f 20 6f 20 43 68 61 74 47 50 54 20 65 20
  //   6f 20 47 65 6d 69 6e 69 21 a
endmodule

// D23
module Detector_23 (
  input  [6:0] Char_In,
  input  Clock,
  input  Reset_Externo,
  output Frase_Detectada
);

  wire and_1_out, comparator_2_eq, comparator_3_eq, not_1_out, not_2_out, or_1_out;
  wire [6:0] counter_1_q, rom_1_data;

  Counter #(.width(7), .max('h7f)) counter_1 (
    .count(not_2_out), .Q(counter_1_q), .clk(Clock), .clr(or_1_out));  // open: load, D, carry
  or or_1 (or_1_out, Reset_Externo, and_1_out, Frase_Detectada);
  and and_1 (and_1_out, not_1_out, not_2_out);
  Comparator #(.width(7)) comparator_1 (.a(counter_1_q), .b(7'b0010001), .eq(Frase_Detectada));  // open: gt, lt
  ROM #(.addrWidth(7), .dataWidth(7)) rom_1 (.addr(counter_1_q), .data(rom_1_data));  // open: sel
  Comparator #(.width(7)) comparator_2 (.a(rom_1_data), .b(Char_In), .eq(comparator_2_eq));  // open: gt, lt
  not not_1 (not_1_out, comparator_2_eq);
  not not_2 (not_2_out, comparator_3_eq);
  Comparator #(.width(7)) comparator_3 (.a(Char_In), .b({7{1'b0}}), .eq(comparator_3_eq));  // open: gt, lt

  // Notes on the sheet:
  //   contents of rom_1 (hex, n*v repeats v):
  //   56 6f 63 65 20 74 65 6d 20 66 69 6c 68 6f 73 3f a
endmodule

// R24
module Resposta_24 (
  input  Iniciar,
  input  Clock,
  output Falando,
  output [6:0] Char_Out
);

  wire comparator_1_eq;
  wire [6:0] counter_1_q, rom_1_data;

  D_Flip_Flop d_ff_1 (.clk(Clock), .Q(Falando), .preset(Iniciar), .reset(comparator_1_eq));  // open: D, Qn, en
  Counter #(.width(7), .max('h7f)) counter_1 (
    .count(Falando), .Q(counter_1_q), .clk(Clock), .clr(comparator_1_eq));  // open: load, D, carry
  Comparator #(.width(7)) comparator_1 (.a(counter_1_q), .b(7'b0100111), .eq(comparator_1_eq));  // open: gt, lt
  ROM #(.addrWidth(7), .dataWidth(7)) rom_1 (.addr(counter_1_q), .data(rom_1_data));  // open: sel
  assign Char_Out = Falando ? rom_1_data : 7'bz;  // Controlled_Buffer controlled_buffer_1

  // Notes on the sheet:
  //   contents of rom_1 (hex, n*v repeats v):
  //   45 75 20 6d 6f 72 72 6f 20 64 65 20 6d 65 64 6f 20 64 65 20 71 75 65 64 61 73 20 64 65 20 65 6e 65
  //   72 67 69 61 21 a
endmodule

// D24
module Detector_24 (
  input  [6:0] Char_In,
  input  Clock,
  input  Reset_Externo,
  output Frase_Detectada
);

  wire and_1_out, comparator_2_eq, comparator_3_eq, not_1_out, not_2_out, or_1_out;
  wire [6:0] counter_1_q, rom_1_data;

  Counter #(.width(7), .max('h7f)) counter_1 (
    .count(not_2_out), .Q(counter_1_q), .clk(Clock), .clr(or_1_out));  // open: load, D, carry
  or or_1 (or_1_out, Reset_Externo, and_1_out, Frase_Detectada);
  and and_1 (and_1_out, not_1_out, not_2_out);
  Comparator #(.width(7)) comparator_1 (.a(counter_1_q), .b(7'b0010111), .eq(Frase_Detectada));  // open: gt, lt
  ROM #(.addrWidth(7), .dataWidth(7)) rom_1 (.addr(counter_1_q), .data(rom_1_data));  // open: sel
  Comparator #(.width(7)) comparator_2 (.a(rom_1_data), .b(Char_In), .eq(comparator_2_eq));  // open: gt, lt
  not not_1 (not_1_out, comparator_2_eq);
  Comparator #(.width(7)) comparator_3 (.a(Char_In), .b({7{1'b0}}), .eq(comparator_3_eq));  // open: gt, lt
  not not_2 (not_2_out, comparator_3_eq);

  // Notes on the sheet:
  //   contents of rom_1 (hex, n*v repeats v):
  //   51 75 61 6c 20 6f 20 73 65 75 20 6d 61 69 6f 72 20 6d 65 64 6f 3f a
endmodule

// R25
module Resposta_25 (
  input  Iniciar,
  input  Clock,
  output Falando,
  output [6:0] Char_Out
);

  wire comparator_1_eq;
  wire [6:0] counter_1_q, rom_1_data;

  D_Flip_Flop d_ff_1 (.clk(Clock), .Q(Falando), .preset(Iniciar), .reset(comparator_1_eq));  // open: D, Qn, en
  Counter #(.width(7), .max('h7f)) counter_1 (
    .count(Falando), .Q(counter_1_q), .clk(Clock), .clr(comparator_1_eq));  // open: load, D, carry
  Comparator #(.width(7)) comparator_1 (.a(counter_1_q), .b(7'b0011011), .eq(comparator_1_eq));  // open: gt, lt
  ROM #(.addrWidth(7), .dataWidth(7)) rom_1 (.addr(counter_1_q), .data(rom_1_data));  // open: sel
  assign Char_Out = Falando ? rom_1_data : 7'bz;  // Controlled_Buffer controlled_buffer_1

  // Notes on the sheet:
  //   contents of rom_1 (hex, n*v repeats v):
  //   45 75 20 61 64 6f 72 6f 20 65 6e 65 72 67 69 61 20 65 6c 65 74 72 69 63 61 21 a
endmodule

// D25
module Detector_25 (
  input  [6:0] Char_In,
  input  Clock,
  input  Reset_Externo,
  output Frase_Detectada
);

  wire and_1_out, comparator_2_eq, comparator_3_eq, not_1_out, not_2_out, or_1_out;
  wire [6:0] counter_1_q, rom_1_data;

  Counter #(.width(7), .max('h7f)) counter_1 (
    .count(not_2_out), .Q(counter_1_q), .clk(Clock), .clr(or_1_out));  // open: load, D, carry
  or or_1 (or_1_out, Reset_Externo, and_1_out, Frase_Detectada);
  and and_1 (and_1_out, not_1_out, not_2_out);
  Comparator #(.width(7)) comparator_1 (.a(counter_1_q), .b(7'b0011010), .eq(Frase_Detectada));  // open: gt, lt
  ROM #(.addrWidth(7), .dataWidth(7)) rom_1 (.addr(counter_1_q), .data(rom_1_data));  // open: sel
  Comparator #(.width(7)) comparator_2 (.a(rom_1_data), .b(Char_In), .eq(comparator_2_eq));  // open: gt, lt
  not not_1 (not_1_out, comparator_2_eq);
  not not_2 (not_2_out, comparator_3_eq);
  Comparator #(.width(7)) comparator_3 (.a(Char_In), .b({7{1'b0}}), .eq(comparator_3_eq));  // open: gt, lt

  // Notes on the sheet:
  //   contents of rom_1 (hex, n*v repeats v):
  //   51 75 61 6c 20 73 75 61 20 63 6f 6d 69 64 61 20 66 61 76 6f 72 69 74 61 3f a
endmodule

// R26
module Resposta_26 (
  input  Iniciar,
  input  Clock,
  output Falando,
  output [6:0] Char_Out
);

  wire comparator_1_eq;
  wire [6:0] counter_1_q, rom_1_data;

  D_Flip_Flop d_ff_1 (.clk(Clock), .Q(Falando), .preset(Iniciar), .reset(comparator_1_eq));  // open: D, Qn, en
  Counter #(.width(7), .max('h7f)) counter_1 (
    .count(Falando), .Q(counter_1_q), .clk(Clock), .clr(comparator_1_eq));  // open: load, D, carry
  Comparator #(.width(7)) comparator_1 (.a(counter_1_q), .b(7'b0110101), .eq(comparator_1_eq));  // open: gt, lt
  ROM #(.addrWidth(7), .dataWidth(7)) rom_1 (.addr(counter_1_q), .data(rom_1_data));  // open: sel
  assign Char_Out = Falando ? rom_1_data : 7'bz;  // Controlled_Buffer controlled_buffer_1

  // Notes on the sheet:
  //   contents of rom_1 (hex, n*v repeats v):
  //   51 75 61 6e 64 6f 20 65 75 20 63 72 65 73 63 65 72 2c 20 71 75 65 72 6f 20 73 65 72 20 75 6d 20 63
  //   6f 6d 70 75 74 61 64 6f 72 20 71 75 61 6e 74 69 63 6f 21 a
endmodule

// D26
module Detector_26 (
  input  [6:0] Char_In,
  input  Clock,
  input  Reset_Externo,
  output Frase_Detectada
);

  wire and_1_out, comparator_2_eq, comparator_3_eq, not_1_out, not_2_out, or_1_out;
  wire [6:0] counter_1_q, rom_1_data;

  Counter #(.width(7), .max('h7f)) counter_1 (
    .count(not_2_out), .Q(counter_1_q), .clk(Clock), .clr(or_1_out));  // open: load, D, carry
  or or_1 (or_1_out, Reset_Externo, and_1_out, Frase_Detectada);
  and and_1 (and_1_out, not_1_out, not_2_out);
  Comparator #(.width(7)) comparator_1 (.a(counter_1_q), .b(7'b0000110), .eq(Frase_Detectada));  // open: gt, lt
  ROM #(.addrWidth(7), .dataWidth(7)) rom_1 (.addr(counter_1_q), .data(rom_1_data));  // open: sel
  not not_1 (not_1_out, comparator_2_eq);
  Comparator #(.width(7)) comparator_2 (.a(rom_1_data), .b(Char_In), .eq(comparator_2_eq));  // open: gt, lt
  not not_2 (not_2_out, comparator_3_eq);
  Comparator #(.width(7)) comparator_3 (.a(Char_In), .b({7{1'b0}}), .eq(comparator_3_eq));  // open: gt, lt

  // Notes on the sheet:
  //   contents of rom_1 (hex, n*v repeats v):
  //   53 6f 6e 68 6f a
endmodule

// R27
module Resposta_27 (
  input  Iniciar,
  input  Clock,
  output Falando,
  output [6:0] Char_Out
);

  wire comparator_1_eq;
  wire [6:0] counter_1_q, rom_1_data;

  D_Flip_Flop d_ff_1 (.clk(Clock), .Q(Falando), .preset(Iniciar), .reset(comparator_1_eq));  // open: D, Qn, en
  Counter #(.width(7), .max('h7f)) counter_1 (
    .count(Falando), .Q(counter_1_q), .clk(Clock), .clr(comparator_1_eq));  // open: load, D, carry
  Comparator #(.width(7)) comparator_1 (.a(counter_1_q), .b(7'b0101011), .eq(comparator_1_eq));  // open: gt, lt
  ROM #(.addrWidth(7), .dataWidth(7)) rom_1 (.addr(counter_1_q), .data(rom_1_data));  // open: sel
  assign Char_Out = Falando ? rom_1_data : 7'bz;  // Controlled_Buffer controlled_buffer_1

  // Notes on the sheet:
  //   contents of rom_1 (hex, n*v repeats v):
  //   4d 65 75 20 6a 6f 67 6f 20 66 61 76 6f 72 69 74 6f 20 65 20 52 65 64 20 44 65 61 64 20 52 65 64 65
  //   6d 70 74 69 6f 6e 20 32 21 a
endmodule

// D27
module Detector_27 (
  input  [6:0] Char_In,
  input  Clock,
  input  Reset_Externo,
  output Frase_Detectada
);

  wire and_1_out, comparator_2_eq, comparator_3_eq, not_1_out, not_2_out, or_1_out;
  wire [6:0] counter_1_q, rom_1_data;

  Counter #(.width(7), .max('h7f)) counter_1 (
    .count(not_2_out), .Q(counter_1_q), .clk(Clock), .clr(or_1_out));  // open: load, D, carry
  or or_1 (or_1_out, Reset_Externo, and_1_out, Frase_Detectada);
  and and_1 (and_1_out, not_1_out, not_2_out);
  Comparator #(.width(7)) comparator_1 (.a(counter_1_q), .b(7'b0011000), .eq(Frase_Detectada));  // open: gt, lt
  ROM #(.addrWidth(7), .dataWidth(7)) rom_1 (.addr(counter_1_q), .data(rom_1_data));  // open: sel
  Comparator #(.width(7)) comparator_2 (.a(rom_1_data), .b(Char_In), .eq(comparator_2_eq));  // open: gt, lt
  not not_1 (not_1_out, comparator_2_eq);
  Comparator #(.width(7)) comparator_3 (.a(Char_In), .b({7{1'b0}}), .eq(comparator_3_eq));  // open: gt, lt
  not not_2 (not_2_out, comparator_3_eq);

  // Notes on the sheet:
  //   contents of rom_1 (hex, n*v repeats v):
  //   51 75 61 6c 20 73 65 75 20 6a 6f 67 6f 20 66 61 76 6f 72 69 74 6f 3f a
endmodule

// R28
module Resposta_28 (
  input  Iniciar,
  input  Clock,
  output Falando,
  output [6:0] Char_Out
);

  wire comparator_1_eq;
  wire [6:0] counter_1_q, rom_1_data;

  D_Flip_Flop d_ff_1 (.clk(Clock), .Q(Falando), .preset(Iniciar), .reset(comparator_1_eq));  // open: D, Qn, en
  Counter #(.width(7), .max('h7f)) counter_1 (
    .count(Falando), .Q(counter_1_q), .clk(Clock), .clr(comparator_1_eq));  // open: load, D, carry
  Comparator #(.width(7)) comparator_1 (.a(counter_1_q), .b(7'b0101000), .eq(comparator_1_eq));  // open: gt, lt
  ROM #(.addrWidth(7), .dataWidth(7)) rom_1 (.addr(counter_1_q), .data(rom_1_data));  // open: sel
  assign Char_Out = Falando ? rom_1_data : 7'bz;  // Controlled_Buffer controlled_buffer_1

  // Notes on the sheet:
  //   contents of rom_1 (hex, n*v repeats v):
  //   4e 6f 20 6d 65 75 20 63 6f 6d 70 75 74 61 64 6f 72 2c 20 65 73 74 61 20 72 6f 64 61 6e 64 6f 20 6e
  //   6f 72 6d 61 6c 21 a
endmodule

// D28
module Detector_28 (
  input  [6:0] Char_In,
  input  Clock,
  input  Reset_Externo,
  output Frase_Detectada
);

  wire and_1_out, comparator_2_eq, comparator_3_eq, not_1_out, not_2_out, or_1_out;
  wire [6:0] counter_1_q, rom_1_data;

  Counter #(.width(7), .max('h7f)) counter_1 (
    .count(not_2_out), .Q(counter_1_q), .clk(Clock), .clr(or_1_out));  // open: load, D, carry
  or or_1 (or_1_out, Reset_Externo, and_1_out, Frase_Detectada);
  and and_1 (and_1_out, not_1_out, not_2_out);
  Comparator #(.width(7)) comparator_1 (.a(counter_1_q), .b(7'b0000100), .eq(Frase_Detectada));  // open: gt, lt
  ROM #(.addrWidth(7), .dataWidth(7)) rom_1 (.addr(counter_1_q), .data(rom_1_data));  // open: sel
  not not_1 (not_1_out, comparator_2_eq);
  Comparator #(.width(7)) comparator_2 (.a(rom_1_data), .b(Char_In), .eq(comparator_2_eq));  // open: gt, lt
  Comparator #(.width(7)) comparator_3 (.a(Char_In), .b({7{1'b0}}), .eq(comparator_3_eq));  // open: gt, lt
  not not_2 (not_2_out, comparator_3_eq);

  // Notes on the sheet:
  //   contents of rom_1 (hex, n*v repeats v):
  //   42 75 67 a
endmodule

// R29
module Resposta_29 (
  input  Iniciar,
  input  Clock,
  output Falando,
  output [6:0] Char_Out
);

  wire comparator_1_eq;
  wire [6:0] counter_1_q, rom_1_data;

  D_Flip_Flop d_ff_1 (.clk(Clock), .Q(Falando), .preset(Iniciar), .reset(comparator_1_eq));  // open: D, Qn, en
  Counter #(.width(7), .max('h7f)) counter_1 (
    .count(Falando), .Q(counter_1_q), .clk(Clock), .clr(comparator_1_eq));  // open: load, D, carry
  Comparator #(.width(7)) comparator_1 (.a(counter_1_q), .b(7'b0001101), .eq(comparator_1_eq));  // open: gt, lt
  ROM #(.addrWidth(7), .dataWidth(7)) rom_1 (.addr(counter_1_q), .data(rom_1_data));  // open: sel
  assign Char_Out = Falando ? rom_1_data : 7'bz;  // Controlled_Buffer controlled_buffer_1

  // Notes on the sheet:
  //   contents of rom_1 (hex, n*v repeats v):
  //   4f 62 72 69 67 61 64 6f 21 20 3c 33 a
endmodule

// D29
module Detector_29 (
  input  [6:0] Char_In,
  input  Clock,
  input  Reset_Externo,
  output Frase_Detectada
);

  wire and_1_out, comparator_2_eq, comparator_3_eq, not_1_out, not_2_out, or_1_out;
  wire [6:0] counter_1_q, rom_1_data;

  Counter #(.width(7), .max('h7f)) counter_1 (
    .count(not_2_out), .Q(counter_1_q), .clk(Clock), .clr(or_1_out));  // open: load, D, carry
  or or_1 (or_1_out, Reset_Externo, and_1_out, Frase_Detectada);
  and and_1 (and_1_out, not_1_out, not_2_out);
  Comparator #(.width(7)) comparator_1 (.a(counter_1_q), .b(7'b0001011), .eq(Frase_Detectada));  // open: gt, lt
  ROM #(.addrWidth(7), .dataWidth(7)) rom_1 (.addr(counter_1_q), .data(rom_1_data));  // open: sel
  Comparator #(.width(7)) comparator_2 (.a(rom_1_data), .b(Char_In), .eq(comparator_2_eq));  // open: gt, lt
  not not_1 (not_1_out, comparator_2_eq);
  Comparator #(.width(7)) comparator_3 (.a(Char_In), .b({7{1'b0}}), .eq(comparator_3_eq));  // open: gt, lt
  not not_2 (not_2_out, comparator_3_eq);

  // Notes on the sheet:
  //   contents of rom_1 (hex, n*v repeats v):
  //   45 75 20 74 65 20 61 6d 6f 21 a
endmodule

// R30
module Resposta_30 (
  input  Iniciar,
  input  Clock,
  output Falando,
  output [6:0] Char_Out
);

  wire comparator_1_eq;
  wire [6:0] counter_1_q, rom_1_data;

  D_Flip_Flop d_ff_1 (.clk(Clock), .Q(Falando), .preset(Iniciar), .reset(comparator_1_eq));  // open: D, Qn, en
  Counter #(.width(7), .max('h7f)) counter_1 (
    .count(Falando), .Q(counter_1_q), .clk(Clock), .clr(comparator_1_eq));  // open: load, D, carry
  Comparator #(.width(7)) comparator_1 (.a(counter_1_q), .b(7'b0100010), .eq(comparator_1_eq));  // open: gt, lt
  ROM #(.addrWidth(7), .dataWidth(7)) rom_1 (.addr(counter_1_q), .data(rom_1_data));  // open: sel
  assign Char_Out = Falando ? rom_1_data : 7'bz;  // Controlled_Buffer controlled_buffer_1

  // Notes on the sheet:
  //   contents of rom_1 (hex, n*v repeats v):
  //   4f 62 72 69 67 61 64 6f 20 70 65 6c 61 20 63 6f 6e 76 65 72 73 61 2c 20 61 74 65 20 6d 61 69 73 21 a
endmodule

// D30
module Detector_30 (
  input  [6:0] Char_In,
  input  Clock,
  input  Reset_Externo,
  output Frase_Detectada
);

  wire and_1_out, comparator_2_eq, comparator_3_eq, not_1_out, not_2_out, or_1_out;
  wire [6:0] counter_1_q, rom_1_data;

  Counter #(.width(7), .max('h7f)) counter_1 (
    .count(not_2_out), .Q(counter_1_q), .clk(Clock), .clr(or_1_out));  // open: load, D, carry
  or or_1 (or_1_out, Reset_Externo, and_1_out, Frase_Detectada);
  and and_1 (and_1_out, not_1_out, not_2_out);
  Comparator #(.width(7)) comparator_1 (.a(counter_1_q), .b(7'b0000110), .eq(Frase_Detectada));  // open: gt, lt
  ROM #(.addrWidth(7), .dataWidth(7)) rom_1 (.addr(counter_1_q), .data(rom_1_data));  // open: sel
  Comparator #(.width(7)) comparator_2 (.a(rom_1_data), .b(Char_In), .eq(comparator_2_eq));  // open: gt, lt
  not not_1 (not_1_out, comparator_2_eq);
  not not_2 (not_2_out, comparator_3_eq);
  Comparator #(.width(7)) comparator_3 (.a(Char_In), .b({7{1'b0}}), .eq(comparator_3_eq));  // open: gt, lt

  // Notes on the sheet:
  //   contents of rom_1 (hex, n*v repeats v):
  //   54 63 68 61 75 a
endmodule
